// Logisim project char.circ as structural Verilog: 2 circuits, main circuit main
module main (
);

  wire Clock_out, n7483_1__14__cout, n7483_2__14__cout;
  wire [7:0] n7483_1__9__s1, register_1_display, register_1_out, register_2_display, register_3_display,
       register_4_display, register_5_display, register_5_out, register_6_display, register_6_out;

  Clock Clock (.out(Clock_out));
  LED led_1 (.in(register_1_out[6]));
  LED led_2 (.in(register_1_out[7]));
  LED led_3 (.in(register_1_out[4]));
  LED led_4 (.in(register_1_out[3]));
  LED led_5 (.in(register_1_out[2]));
  LED led_6 (.in(register_1_out[5]));
  Register register_1 (
    .READ(1'b1), .IN(register_1_out), .WRITE(1'b1), .OUT(register_1_out), .DISPLAY(register_1_display),
    .Clock(Clock_out), .nCLEAR(1'b1));
  Register register_2 (
    .READ(1'b1), .IN(register_1_out), .WRITE(1'b1), .OUT(register_1_out), .DISPLAY(register_2_display),
    .Clock(Clock_out), .nCLEAR(1'b1));
  Register register_3 (
    .READ(1'b1), .IN(register_1_out), .WRITE(1'b1), .OUT(register_1_out), .DISPLAY(register_3_display),
    .Clock(Clock_out), .nCLEAR(1'b1));
  Register register_4 (
    .READ(1'b1), .IN(register_1_out), .WRITE(1'b1), .OUT(register_1_out), .DISPLAY(register_4_display),
    .Clock(Clock_out), .nCLEAR(1'b1));
  LED led_7 (.in(register_1_out[1]));
  LED led_8 (.in(register_1_out[0]));
  LED led_9 (.in(register_1_display[7]));
  LED led_10 (.in(register_1_display[4]));
  LED led_11 (.in(register_1_display[6]));
  LED led_12 (.in(register_1_display[5]));
  LED led_13 (.in(register_2_display[5]));
  LED led_14 (.in(register_2_display[7]));
  LED led_15 (.in(register_2_display[6]));
  LED led_16 (.in(register_2_display[4]));
  LED led_17 (.in(register_3_display[4]));
  LED led_18 (.in(register_3_display[7]));
  LED led_19 (.in(register_3_display[6]));
  LED led_20 (.in(register_3_display[5]));
  LED led_21 (.in(register_4_display[7]));
  LED led_22 (.in(register_4_display[6]));
  LED led_23 (.in(register_4_display[5]));
  LED led_24 (.in(register_4_display[4]));
  LED led_25 (.in(register_1_display[0]));
  LED led_26 (.in(register_1_display[3]));
  LED led_27 (.in(register_1_display[2]));
  LED led_28 (.in(register_1_display[1]));
  LED led_29 (.in(register_2_display[2]));
  LED led_30 (.in(register_2_display[1]));
  LED led_31 (.in(register_2_display[0]));
  LED led_32 (.in(register_2_display[3]));
  LED led_33 (.in(register_3_display[1]));
  LED led_34 (.in(register_3_display[2]));
  LED led_35 (.in(register_3_display[3]));
  LED led_36 (.in(register_3_display[0]));
  LED led_37 (.in(register_4_display[1]));
  LED led_38 (.in(register_4_display[0]));
  LED led_39 (.in(register_4_display[3]));
  LED led_40 (.in(register_4_display[2]));
  _7_Segment_Display u_7_segment_display_1 ();  // open: g, f, a, b, e, d, c, dp
  Register register_5 (
    .READ(1'b1), .IN(register_1_out), .WRITE(1'b0), .OUT(register_5_out), .DISPLAY(register_5_display),
    .Clock(Clock_out), .nCLEAR(1'b1));
  LED led_41 (.in(register_6_display[7]));
  Register register_6 (
    .READ(1'b1), .IN(register_1_out), .WRITE(1'b0), .OUT(register_6_out), .DISPLAY(register_6_display),
    .Clock(Clock_out), .nCLEAR(1'b1));
  LED led_42 (.in(register_6_display[6]));
  LED led_43 (.in(register_5_display[4]));
  LED led_44 (.in(register_5_display[5]));
  LED led_45 (.in(register_5_display[7]));
  LED led_46 (.in(register_5_display[6]));
  _7483 u_7483_1 (
    ._1__A4(register_5_out[3]), ._2__S3(n7483_1__9__s1[2]), ._3__A3(register_5_out[2]),
    ._4__B3(register_6_out[3]), ._5__Vcc(1'b1), ._6__S2(n7483_1__9__s1[1]), ._7__B2(register_6_out[1]),
    ._8__A2(register_5_out[1]), ._16__B4(register_6_out[2]), ._15__S4(n7483_1__9__s1[3]),
    ._14__Cout(n7483_1__14__cout), ._13__Cin(1'b0), ._12__GND(1'b0), ._11__B1(register_6_out[0]),
    ._10__A1(register_5_out[0]), ._9__S1(n7483_1__9__s1[0]));
  LED led_47 (.in(register_6_display[3]));
  LED led_48 (.in(register_6_display[2]));
  LED led_49 (.in(register_6_display[4]));
  LED led_50 (.in(register_6_display[5]));
  LED led_51 (.in(register_5_display[2]));
  LED led_52 (.in(register_5_display[1]));
  LED led_53 (.in(register_5_display[0]));
  LED led_54 (.in(register_5_display[3]));
  LED led_55 (.in(register_6_display[1]));
  LED led_56 (.in(register_6_display[0]));
  _7483 u_7483_2 (
    ._1__A4(register_5_out[7]), ._2__S3(n7483_1__9__s1[6]), ._3__A3(register_5_out[6]),
    ._4__B3(register_6_out[6]), ._5__Vcc(1'b1), ._6__S2(n7483_1__9__s1[5]), ._7__B2(register_6_out[5]),
    ._8__A2(register_5_out[5]), ._16__B4(register_6_out[7]), ._15__S4(n7483_1__9__s1[7]),
    ._14__Cout(n7483_2__14__cout), ._13__Cin(n7483_1__14__cout), ._12__GND(1'b0),
    ._11__B1(register_6_out[4]), ._10__A1(register_5_out[4]), ._9__S1(n7483_1__9__s1[4]));
  LED led_57 (.in(n7483_2__14__cout));
  _27245 u_27245_1 (
    .DIR(1'b1), .A0(n7483_1__9__s1[0]), .A1(n7483_1__9__s1[1]), .A2(n7483_1__9__s1[2]),
    .A3(n7483_1__9__s1[3]), .A4(n7483_1__9__s1[4]), .A5(n7483_1__9__s1[5]), .A6(n7483_1__9__s1[6]),
    .A7(n7483_1__9__s1[7]), .B0(register_1_out[0]), .B1(register_1_out[1]), .B2(register_1_out[2]),
    .B3(register_1_out[3]), .B4(register_1_out[4]), .B5(register_1_out[5]), .B6(register_1_out[6]),
    .B7(register_1_out[7]), .ENABLE(1'b1));

  // Notes on the sheet:
  //   Power
  //   !Clear
  //   Data Bus
  //   Regiser: A
  //   Regiser: B
  //   Regiser: C
  //   Regiser: D
  //   Register: mB
  //   Register: mA
  //   Joseph A. Boyle
endmodule

module Register (
  input  READ,
  input  [7:0] IN,
  input  nCLEAR,
  input  Clock,
  input  WRITE,
  output [7:0] DISPLAY,
  output [7:0] OUT
);

  wire n27245_1_b0, n27245_1_b1, n27245_1_b2, n27245_1_b3, n27245_1_b4, n27245_1_b5, n27245_1_b6, n27245_1_b7;

  _27245 u_27245_1 (
    .DIR(1'b1), .A0(IN[0]), .A1(IN[1]), .A2(IN[2]), .A3(IN[3]), .A4(IN[4]), .A5(IN[5]), .A6(IN[6]),
    .A7(IN[7]), .B0(n27245_1_b0), .B1(n27245_1_b1), .B2(n27245_1_b2), .B3(n27245_1_b3), .B4(n27245_1_b4),
    .B5(n27245_1_b5), .B6(n27245_1_b6), .B7(n27245_1_b7), .ENABLE(READ));
  _27245 u_27245_2 (
    .DIR(1'b1), .A0(DISPLAY[0]), .A1(DISPLAY[1]), .A2(DISPLAY[2]), .A3(DISPLAY[3]), .A4(DISPLAY[4]),
    .A5(DISPLAY[5]), .A6(DISPLAY[6]), .A7(DISPLAY[7]), .B0(OUT[0]), .B1(OUT[1]), .B2(OUT[2]), .B3(OUT[3]),
    .B4(OUT[4]), .B5(OUT[5]), .B6(OUT[6]), .B7(OUT[7]), .ENABLE(WRITE));
  // _74273 74273_1: pin names not known; wires that end beside it: n27245_1_b0, n27245_1_b1, n27245_1_b2, n27245_1_b3, n27245_1_b4, n27245_1_b5, n27245_1_b6, n27245_1_b7, nCLEAR, Clock, DISPLAY[0], DISPLAY[1], DISPLAY[2], DISPLAY[3], DISPLAY[4], DISPLAY[5], DISPLAY[6], DISPLAY[7]
endmodule
